// Logisim project 1.circ as structural Verilog: 1 circuit, main circuit main
module main (
  input  A,
  input  B,
  input  Vem_1,
  output S,
  output Vai_1
);

  wire and_1_out, and_2_out, not_1_out, or_1_out, xor_1_out;

  not not_1 (not_1_out, A);
  xor xor_1 (xor_1_out, A, B);
  or or_1 (or_1_out, B, Vem_1);
  and and_1 (and_1_out, or_1_out, not_1_out);
  buf and_2 (and_2_out, Vem_1);  // AND_Gate
  xor xor_2 (S, xor_1_out, Vem_1);
  or or_2 (Vai_1, and_1_out, and_2_out);
endmodule
