// Logisim project projetoaula.circ as structural Verilog: 5 circuits, main circuit add_1bits
module add_1bits (
  input  A,
  input  B,
  input  Vem_1,
  output S,
  output Vai_1
);

  wire and_1_out, and_2_out, or_1_out, xor_1_out;

  xor xor_1 (xor_1_out, A, B);
  or or_1 (or_1_out, B, Vem_1);
  and and_1 (and_1_out, B, Vem_1);
  xor xor_2 (S, xor_1_out, Vem_1);
  and and_2 (and_2_out, or_1_out, A);
  or or_2 (Vai_1, and_2_out, and_1_out);
endmodule

module sub_1bits (
  input  A,
  input  B,
  input  Vem_1,
  output S,
  output Vai_1
);

  wire and_1_out, and_2_out, not_1_out, or_1_out, xor_1_out;

  not not_1 (not_1_out, A);
  xor xor_1 (xor_1_out, A, B);
  or or_1 (or_1_out, B, Vem_1);
  and and_1 (and_1_out, B, Vem_1);
  xor xor_2 (S, xor_1_out, Vem_1);
  and and_2 (and_2_out, or_1_out, not_1_out);
  or or_2 (Vai_1, and_2_out, and_1_out);
endmodule

module somador_4bits (
  input  [3:0] B,
  input  [3:0] A,
  input  in_3,
  output out_4,
  output [3:0] out_5
);

  wire add_1bits_2_vai_1, add_1bits_3_vai_1, add_1bits_4_vai_1;

  add_1bits add_1bits_1 (.A(A[3]), .B(B[3]), .Vem_1(add_1bits_2_vai_1), .S(out_5[3]), .Vai_1(out_4));
  add_1bits add_1bits_2 (.A(A[2]), .B(B[2]), .Vem_1(add_1bits_3_vai_1), .S(out_5[2]), .Vai_1(add_1bits_2_vai_1));
  add_1bits add_1bits_3 (.A(A[1]), .B(B[1]), .Vem_1(add_1bits_4_vai_1), .S(out_5[1]), .Vai_1(add_1bits_3_vai_1));
  add_1bits add_1bits_4 (.A(A[0]), .B(B[0]), .Vem_1(in_3), .S(out_5[0]), .Vai_1(add_1bits_4_vai_1));
endmodule

module subtrator_4bits (
  input  [3:0] A,
  input  [3:0] B,
  input  in_3,
  output out_4,
  output [3:0] out_5
);

  wire sub_1bits_2_vai_1, sub_1bits_3_vai_1, sub_1bits_4_vai_1;

  sub_1bits sub_1bits_1 (.A(A[3]), .B(B[3]), .Vem_1(sub_1bits_2_vai_1), .S(out_5[3]), .Vai_1(out_4));
  sub_1bits sub_1bits_2 (.A(A[2]), .B(B[2]), .Vem_1(sub_1bits_3_vai_1), .S(out_5[2]), .Vai_1(sub_1bits_2_vai_1));
  sub_1bits sub_1bits_3 (.A(A[1]), .B(B[1]), .Vem_1(sub_1bits_4_vai_1), .S(out_5[1]), .Vai_1(sub_1bits_3_vai_1));
  sub_1bits sub_1bits_4 (.A(A[0]), .B(B[0]), .Vem_1(in_3), .S(out_5[0]), .Vai_1(sub_1bits_4_vai_1));
endmodule

module \final  (
  input  [3:0] A,
  input  [3:0] B,
  output Overflow,
  output Overflow_2,
  output [3:0] S,
  output [3:0] S_2
);

  somador_4bits somador_4bits_1 (.B(B), .A(A), .out_4(Overflow), .out_5(S), .in_3(1'b0));
  subtrator_4bits subtrator_4bits_1 (.A(A), .B(B), .out_4(Overflow_2), .out_5(S_2), .in_3(1'b0));
endmodule
